// Logisim project ALU8.circ as structural Verilog: 10 circuits, main circuit main
module main (
  input  [7:0] A,
  input  [7:0] B,
  input  Cin,
  input  [3:0] Op,
  output Cout,
  output ZF,
  output SF,
  output OF,
  output [7:0] F
);

  ALU alu_1 (.A(A), .B(B), .Cin(Cin), .Cout(Cout), .OF(ZF), .ZF(SF), .SF(OF), .Op(Op), .F(F));
endmodule

module ALU (
  input  [7:0] A,
  input  [7:0] B,
  input  Cin,
  input  [3:0] Op,
  output ZF,
  output Cout,
  output OF,
  output SF,
  output [7:0] F
);

  wire [7:0] ADD_f, AND_f, SHIFT_LEFT_f, SHIFT_RIGHT_f, SUB_f, undriven, XOR_f;

  addl ADD (.Cin(Cin), .A(A), .B(B), .F(ADD_f));  // open: OF, Cout
  subl SUB (.Cin(Cin), .B(B), .A(A), .F(SUB_f));  // open: Cout, OF
  andl AND (.A(A), .B(B), .F(AND_f));  // open: OF
  xorl XOR (.A(A), .B(undriven), .F(XOR_f));  // open: OF
  asrl SHIFT_RIGHT (.A(A), .F(SHIFT_RIGHT_f));  // open: Cout, OF
  lsll SHIFT_LEFT (.A(A), .F(SHIFT_LEFT_f));  // open: Cout, OF
  Multiplexer #(.select(4), .width(8), .enable("false")) multiplexer_1 (
    .in0(ADD_f), .in1(SUB_f), .in2(AND_f), .in3(XOR_f), .in4(SHIFT_RIGHT_f), .in5(SHIFT_LEFT_f),
    .out({8{F[7]}}), .sel(Op));  // open: in6, in7, in8, in9, in10, in11, in12, in13, in14, in15

  assign F[6:0] = {7{F[7]}};
  assign SF = F[7];
  assign ZF = F[7];
endmodule

module andl (
  input  [7:0] A,
  input  [7:0] B,
  output OF,
  output [7:0] F
);

  assign F = A & B;  // AND_Gate and_1, 8 bits wide

  assign OF = 1'b0;
endmodule

module xorl (
  input  [7:0] A,
  input  [7:0] B,
  output OF,
  output [7:0] F
);

  assign F = A ^ B;  // XOR_Gate xor_1, 8 bits wide

  assign OF = 1'b0;
endmodule

module addl (
  input  Cin,
  input  [7:0] B,
  input  [7:0] A,
  output [7:0] F,
  output Cout,
  output OF
);

  wire adder_1_cout, adder_2_cout, adder_3_cout, adder_4_cout, adder_5_cout, adder_6_cout, adder_7_cout;

  adder adder_1 (.A(A[1]), .B(B[1]), .Cin(adder_2_cout), .Out(F[1]), .Cout(adder_1_cout));
  adder adder_2 (.A(A[0]), .B(B[0]), .Cin(Cin), .Out(F[0]), .Cout(adder_2_cout));
  adder adder_3 (.A(A[3]), .B(B[3]), .Cin(adder_4_cout), .Out(F[3]), .Cout(adder_3_cout));
  adder adder_4 (.A(A[2]), .B(B[2]), .Cin(adder_1_cout), .Out(F[2]), .Cout(adder_4_cout));
  adder adder_5 (.A(A[4]), .B(B[4]), .Cin(adder_3_cout), .Out(F[4]), .Cout(adder_5_cout));
  adder adder_6 (.A(A[5]), .B(B[5]), .Cin(adder_5_cout), .Out(F[5]), .Cout(adder_6_cout));
  adder adder_7 (.A(A[6]), .B(B[6]), .Cin(adder_6_cout), .Out(F[6]), .Cout(adder_7_cout));
  adder adder_8 (.A(A[7]), .B(B[7]), .Cin(adder_7_cout), .Out(F[7]), .Cout(Cout));

  assign OF = Cout;
endmodule

module subl (
  input  Cin,
  input  [7:0] B,
  input  [7:0] A,
  output [7:0] F,
  output Cout,
  output OF
);

  wire subtracter_1_cout, subtracter_2_cout, subtracter_3_cout, subtracter_4_cout, subtracter_5_cout,
       subtracter_6_cout, subtracter_7_cout;

  subtracter subtracter_1 (.A(A[1]), .B(B[1]), .Cin(subtracter_2_cout), .Out(F[1]), .Cout(subtracter_1_cout));
  subtracter subtracter_2 (.A(A[0]), .B(B[0]), .Cin(Cin), .Out(F[0]), .Cout(subtracter_2_cout));
  subtracter subtracter_3 (.A(A[3]), .B(B[3]), .Cin(subtracter_4_cout), .Out(F[3]), .Cout(subtracter_3_cout));
  subtracter subtracter_4 (.A(A[2]), .B(B[2]), .Cin(subtracter_1_cout), .Out(F[2]), .Cout(subtracter_4_cout));
  subtracter subtracter_5 (.A(A[4]), .B(B[4]), .Cin(subtracter_3_cout), .Out(F[4]), .Cout(subtracter_5_cout));
  subtracter subtracter_6 (.A(A[6]), .B(B[6]), .Cin(subtracter_7_cout), .Out(F[6]), .Cout(subtracter_6_cout));
  subtracter subtracter_7 (.A(A[5]), .B(B[5]), .Cin(subtracter_5_cout), .Out(F[5]), .Cout(subtracter_7_cout));
  subtracter subtracter_8 (.A(A[7]), .B(B[7]), .Cin(subtracter_6_cout), .Out(F[7]), .Cout(Cout));

  assign OF = Cout;
endmodule

module asrl (
  input  [7:0] A,
  output Cout,
  output OF,
  output [7:0] F
);
endmodule

module lsll (
  input  [7:0] A,
  output Cout,
  output OF,
  output [7:0] F
);
endmodule

module adder (
  input  A,
  input  B,
  input  Cin,
  output Out,
  output Cout
);

  wire and_1_out, and_2_out, xor_1_out;

  xor xor_1 (xor_1_out, A, B);
  and and_1 (and_1_out, xor_1_out, Cin);
  and and_2 (and_2_out, A, B);
  xor xor_2 (Out, xor_1_out, Cin);
  or or_1 (Cout, and_1_out, and_2_out);
endmodule

module subtracter (
  input  A,
  input  B,
  input  Cin,
  output Out,
  output Cout
);

  wire and_1_out, and_2_out, not_1_out, not_2_out, xor_1_out;

  xor xor_1 (xor_1_out, A, B);
  not not_1 (not_1_out, B);
  and and_1 (and_1_out, xor_1_out, Cin);
  not not_2 (not_2_out, and_1_out);
  and and_2 (and_2_out, A, not_1_out);
  xor xor_2 (Out, xor_1_out, Cin);
  or or_1 (Cout, not_2_out, and_2_out);
endmodule
